// Logisim project p3_final.circ as structural Verilog: 12 circuits, main circuit main
module main (
  input  in_1,
  output [31:0] Instr,
  output RegWrite,
  output [4:0] RegAddr,
  output [31:0] RegData,
  output MemWrite,
  output [4:0] MemAddr,
  output [31:0] MemData
);

  wire alusrc, BGEZ, BGTZ, BLEZ, BLTZ, branch, branchlogic_1_out_12, clk, ctrl_1_isbgez, ctrl_1_isbltz,
       isbeq, ISBGEZ, ISBGTZ, ISBLEZ, ISBLTZ, not_1_out, zero;
  wire [1:0] aluop, dmdatactrl, dmoutctrl, extop, npcop, regdst, shiftop;
  wire [2:0] memtoreg;
  wire [31:0] aluout, bit_extender_1_out, \byte , byte_1_byteout, dm, dmdatain, dmout, extout, half,
       halfword_1_halfword, multiplexer_3_out, npc, pc4, rd1, shiftout;

  Clock clock_1 (.out(clk));
  BRANCHLOGIC branchlogic_1 (
    .out_12(branchlogic_1_out_12), .isbgtz(ISBLTZ), .isblez(ISBLEZ), .isbgez(ISBGEZ), .isbgtz_2(ISBGTZ),
    .isbeq(isbeq), .bltz(BLTZ), .blez(BLEZ), .bgez(BGEZ), .bgtz(BGTZ), .zero(zero), .branch(branch));
  ctrl ctrl_1 (
    .op(Instr[31:26]), .funct(Instr[5:0]), .isbeq(isbeq), .isbgtz(ISBGTZ), .isbgez(ctrl_1_isbgez),
    .isbltz(ctrl_1_isbltz), .isblez(ISBLTZ), .dmdatactrl(dmdatactrl), .dmoutctrl(dmoutctrl), .regdst(regdst),
    .regwrite(RegWrite), .alusrc(alusrc), .aluop(aluop), .memwrite(MemWrite), .extop(extop), .npcop(npcop),
    .branch(branch), .memtoreg(memtoreg), .sftop(shiftop));
  IFU ifu_1 (.clk(clk), .reset(in_1), .branch(branchlogic_1_out_12), .npc(npc), .Instr(Instr), .pc4(pc4));
  and and_1 (ISBGEZ, Instr[16], ctrl_1_isbgez);
  CMP cmp_1 (.A(rd1), .B(MemData), .BGTZ(BGTZ), .BGEZ(BGEZ), .BLEZ(BLEZ), .BLTZ(BLTZ));
  and and_2 (ISBLEZ, not_1_out, ctrl_1_isbltz);
  not not_1 (not_1_out, Instr[16]);
  SHIFT shift (.shiftop(shiftop), .shamt(Instr[10:6]), .data(MemData), .shiftdata(shiftout));
  assign bit_extender_1_out = {{31{1'b0}}, BLTZ};  // Bit_Extender bit_extender_1
  Multiplexer #(.select(2), .width(5)) multiplexer_1 (
    .in0(Instr[15:11]), .in1(Instr[20:16]), .in2({5{1'b1}}), .out(RegAddr), .sel(regdst));  // open: in3, en
  NPC u_npc (.npcop(npcop), .pc4(pc4), .extout(extout), .rd1(rd1), .instr(Instr), .npc(npc));
  GPR gpr_1 (
    .clk(clk), .reset(in_1), .WE(RegWrite), .A1(Instr[25:21]), .A2(Instr[20:16]), .A3(RegAddr), .WD(RegData),
    .RD1(rd1), .RD2(MemData));
  Multiplexer #(.select(3), .width(32)) multiplexer_2 (
    .in0({aluout[31:7], MemAddr, aluout[1:0]}), .in1(dmout), .in2(extout), .in3(pc4), .in4(shiftout),
    .in5(bit_extender_1_out), .out(RegData), .sel(memtoreg));  // open: in6, in7, en
  EXT ext (.A(Instr[15:0]), .Extop(extop), .B(extout));
  Multiplexer #(.width(32)) multiplexer_3 (
    .in0(MemData), .in1(extout), .out(multiplexer_3_out), .sel(alusrc));  // open: en
  ALU alu_1 (
    .a1(rd1), .a2(multiplexer_3_out), .aluop(aluop), .zero(zero),
    .aluout({aluout[31:7], MemAddr, aluout[1:0]}));  // open: sign, unsign
  halfword halfword_1 (
    .addr(aluout[1:0]), .dmout(dm), .data(MemData), .halfword(halfword_1_halfword), .fordmdata(half));
  \byte  byte_1 (.addr(aluout[1:0]), .dmout(dm), .data(MemData), .byteout(byte_1_byteout), .fordmdata(\byte ));
  Multiplexer #(.select(2), .width(32)) multiplexer_4 (
    .in0(MemData), .in1(half), .in2(\byte ), .out(dmdatain), .sel(dmdatactrl));  // open: in3, en
  RAM #(.addrWidth(5), .dataWidth(32), .bus("separate")) ram_1 (
    .addr(MemAddr), .din(dmdatain), .data(dm), .str(MemWrite), .clk(clk), .clr(in_1));  // open: sel, ld
  Multiplexer #(.select(2), .width(32)) multiplexer_5 (
    .in0(dm), .in1(halfword_1_halfword), .in2(byte_1_byteout), .out(dmout), .sel(dmoutctrl));  // open: in3, en
  // Probe on dmout

  // Other names for the same wires on the sheet: aluout[6:2] = MemAddr; clr = in_1; funct[5:0] = Instr[5:0];
  //   imm[15:0] = Instr[15:0]; opcode[5:0] = Instr[31:26]; rd[4:0] = Instr[15:11]; rd2[31:0] = MemData;
  //   rs[4:0] = Instr[25:21]; rt[4:0] = Instr[20:16]; shamt[4:0] = Instr[10:6]
endmodule

// ifu
module IFU (
  input  clk,
  input  reset,
  input  branch,
  input  [31:0] npc,
  output [31:0] Instr,
  output [31:0] pc4
);

  wire [11:0] register_1_q;
  wire [31:0] multiplexer_1_out;

  Multiplexer #(.width(32)) multiplexer_1 (.in0(pc4), .in1(npc), .out(multiplexer_1_out), .sel(branch));  // open: en
  Register #(.width(12)) register_1 (
    .D(multiplexer_1_out[11:0]), .Q(register_1_q), .clk(clk), .clr(reset));  // open: en
  Adder #(.width(32)) adder_1 (.a({20'h3, register_1_q}), .b(32'h4), .out(pc4));  // open: cin, cout
  ROM #(.addrWidth(5), .dataWidth(32)) rom_1 (.addr(register_1_q[6:2]), .data(Instr));  // open: sel

  // Notes on the sheet:
  //   contents of rom_1 (hex, n*v repeats v):
  //   36100008 ae10fffc
endmodule

// gpr
module GPR (
  input  clk,
  input  reset,
  input  WE,
  input  [4:0] A1,
  input  [4:0] A2,
  input  [4:0] A3,
  input  [31:0] WD,
  output [31:0] RD1,
  output [31:0] RD2
);

  wire [4:0] multiplexer_1_out;
  wire [7:0] decoder_1_out0, decoder_1_out8, decoder_1_out16, decoder_1_out24;
  wire [31:0] multiplexer_2_out, multiplexer_3_out, multiplexer_4_out, multiplexer_5_out, multiplexer_6_out,
       multiplexer_7_out, multiplexer_8_out, multiplexer_9_out, register_1_q, register_2_q, register_3_q,
       register_4_q, register_5_q, register_6_q, register_7_q, register_8_q, register_9_q, register_10_q,
       register_11_q, register_12_q, register_13_q, register_14_q, register_15_q, register_16_q,
       register_17_q, register_18_q, register_19_q, register_20_q, register_21_q, register_22_q,
       register_23_q, register_24_q, register_25_q, register_26_q, register_27_q, register_28_q,
       register_29_q, register_30_q, register_31_q, register_32_q;

  Decoder #(.select(5)) decoder_1 (
    .out0(decoder_1_out0[0]), .out1(decoder_1_out0[1]), .out2(decoder_1_out0[2]), .out3(decoder_1_out0[3]),
    .out4(decoder_1_out0[4]), .out5(decoder_1_out0[5]), .out6(decoder_1_out0[6]), .out7(decoder_1_out0[7]),
    .out8(decoder_1_out8[0]), .out9(decoder_1_out8[1]), .out10(decoder_1_out8[2]), .out11(decoder_1_out8[3]),
    .out12(decoder_1_out8[4]), .out13(decoder_1_out8[5]), .out14(decoder_1_out8[6]),
    .out15(decoder_1_out8[7]), .out16(decoder_1_out16[0]), .out17(decoder_1_out16[1]),
    .out18(decoder_1_out16[2]), .out19(decoder_1_out16[3]), .out20(decoder_1_out16[4]),
    .out21(decoder_1_out16[5]), .out22(decoder_1_out16[6]), .out23(decoder_1_out16[7]),
    .out24(decoder_1_out24[0]), .out25(decoder_1_out24[1]), .out26(decoder_1_out24[2]),
    .out27(decoder_1_out24[3]), .out28(decoder_1_out24[4]), .out29(decoder_1_out24[5]),
    .out30(decoder_1_out24[6]), .out31(decoder_1_out24[7]), .sel(multiplexer_1_out));  // open: en
  Multiplexer #(.width(5)) multiplexer_1 (.in0({5{1'b0}}), .in1(A3), .out(multiplexer_1_out), .sel(WE));  // open: en
  Register #(.width(32)) register_1 (.D({32{1'b0}}), .en(decoder_1_out0[0]), .Q(register_1_q), .clk(clk), .clr(reset));
  Register #(.width(32)) register_2 (.D(WD), .en(decoder_1_out8[0]), .Q(register_2_q), .clk(clk), .clr(reset));
  Register #(.width(32)) register_3 (.D(WD), .en(decoder_1_out16[0]), .Q(register_3_q), .clk(clk), .clr(reset));
  Register #(.width(32)) register_4 (.D(WD), .en(decoder_1_out24[0]), .Q(register_4_q), .clk(clk), .clr(reset));
  Register #(.width(32)) register_5 (.D(WD), .en(decoder_1_out0[1]), .Q(register_5_q), .clk(clk), .clr(reset));
  Register #(.width(32)) register_6 (.D(WD), .en(decoder_1_out8[1]), .Q(register_6_q), .clk(clk), .clr(reset));
  Register #(.width(32)) register_7 (.D(WD), .en(decoder_1_out16[1]), .Q(register_7_q), .clk(clk), .clr(reset));
  Register #(.width(32)) register_8 (.D(WD), .en(decoder_1_out24[1]), .Q(register_8_q), .clk(clk), .clr(reset));
  Register #(.width(32)) register_9 (.D(WD), .en(decoder_1_out0[2]), .Q(register_9_q), .clk(clk), .clr(reset));
  Register #(.width(32)) register_10 (.D(WD), .en(decoder_1_out8[2]), .Q(register_10_q), .clk(clk), .clr(reset));
  Register #(.width(32)) register_11 (.D(WD), .en(decoder_1_out16[2]), .Q(register_11_q), .clk(clk), .clr(reset));
  Register #(.width(32)) register_12 (.D(WD), .en(decoder_1_out24[2]), .Q(register_12_q), .clk(clk), .clr(reset));
  Register #(.width(32)) register_13 (.D(WD), .en(decoder_1_out0[3]), .Q(register_13_q), .clk(clk), .clr(reset));
  Register #(.width(32)) register_14 (.D(WD), .en(decoder_1_out8[3]), .Q(register_14_q), .clk(clk), .clr(reset));
  Register #(.width(32)) register_15 (.D(WD), .en(decoder_1_out16[3]), .Q(register_15_q), .clk(clk), .clr(reset));
  Register #(.width(32)) register_16 (.D(WD), .en(decoder_1_out24[3]), .Q(register_16_q), .clk(clk), .clr(reset));
  Register #(.width(32)) register_17 (.D(WD), .en(decoder_1_out0[4]), .Q(register_17_q), .clk(clk), .clr(reset));
  Register #(.width(32)) register_18 (.D(WD), .en(decoder_1_out8[4]), .Q(register_18_q), .clk(clk), .clr(reset));
  Register #(.width(32)) register_19 (.D(WD), .en(decoder_1_out16[4]), .Q(register_19_q), .clk(clk), .clr(reset));
  Register #(.width(32)) register_20 (.D(WD), .en(decoder_1_out24[4]), .Q(register_20_q), .clk(clk), .clr(reset));
  Register #(.width(32)) register_21 (.D(WD), .en(decoder_1_out0[5]), .Q(register_21_q), .clk(clk), .clr(reset));
  Register #(.width(32)) register_22 (.D(WD), .en(decoder_1_out8[5]), .Q(register_22_q), .clk(clk), .clr(reset));
  Register #(.width(32)) register_23 (.D(WD), .en(decoder_1_out16[5]), .Q(register_23_q), .clk(clk), .clr(reset));
  Register #(.width(32)) register_24 (.D(WD), .en(decoder_1_out24[5]), .Q(register_24_q), .clk(clk), .clr(reset));
  Register #(.width(32)) register_25 (.D(WD), .en(decoder_1_out0[6]), .Q(register_25_q), .clk(clk), .clr(reset));
  Register #(.width(32)) register_26 (.D(WD), .en(decoder_1_out8[6]), .Q(register_26_q), .clk(clk), .clr(reset));
  Register #(.width(32)) register_27 (.D(WD), .en(decoder_1_out16[6]), .Q(register_27_q), .clk(clk), .clr(reset));
  Register #(.width(32)) register_28 (.D(WD), .en(decoder_1_out24[6]), .Q(register_28_q), .clk(clk), .clr(reset));
  Register #(.width(32)) register_29 (.D(WD), .en(decoder_1_out0[7]), .Q(register_29_q), .clk(clk), .clr(reset));
  Register #(.width(32)) register_30 (.D(WD), .en(decoder_1_out8[7]), .Q(register_30_q), .clk(clk), .clr(reset));
  Register #(.width(32)) register_31 (.D(WD), .en(decoder_1_out16[7]), .Q(register_31_q), .clk(clk), .clr(reset));
  Register #(.width(32)) register_32 (.D(WD), .en(decoder_1_out24[7]), .Q(register_32_q), .clk(clk), .clr(reset));
  Multiplexer #(.select(3), .width(32)) multiplexer_2 (
    .in0(register_1_q), .in1(register_5_q), .in2(register_9_q), .in3(register_13_q), .in4(register_17_q),
    .in5(register_21_q), .in6(register_25_q), .in7(register_29_q), .out(multiplexer_2_out), .sel(A1[2:0]));  // open: en
  Multiplexer #(.select(3), .width(32)) multiplexer_3 (
    .in0(register_2_q), .in1(register_6_q), .in2(register_10_q), .in3(register_14_q), .in4(register_18_q),
    .in5(register_22_q), .in6(register_26_q), .in7(register_30_q), .out(multiplexer_3_out), .sel(A1[2:0]));  // open: en
  Multiplexer #(.select(3), .width(32)) multiplexer_4 (
    .in0(register_3_q), .in1(register_7_q), .in2(register_11_q), .in3(register_15_q), .in4(register_19_q),
    .in5(register_23_q), .in6(register_27_q), .in7(register_31_q), .out(multiplexer_4_out), .sel(A1[2:0]));  // open: en
  Multiplexer #(.select(3), .width(32)) multiplexer_5 (
    .in0(register_4_q), .in1(register_8_q), .in2(register_12_q), .in3(register_16_q), .in4(register_20_q),
    .in5(register_24_q), .in6(register_28_q), .in7(register_32_q), .out(multiplexer_5_out), .sel(A1[2:0]));  // open: en
  Multiplexer #(.select(3), .width(32)) multiplexer_6 (
    .in0(register_1_q), .in1(register_5_q), .in2(register_9_q), .in3(register_13_q), .in4(register_17_q),
    .in5(register_21_q), .in6(register_25_q), .in7(register_29_q), .out(multiplexer_6_out), .sel(A2[2:0]));  // open: en
  Multiplexer #(.select(3), .width(32)) multiplexer_7 (
    .in0(register_2_q), .in1(register_6_q), .in2(register_10_q), .in3(register_14_q), .in4(register_18_q),
    .in5(register_22_q), .in6(register_26_q), .in7(register_30_q), .out(multiplexer_7_out), .sel(A2[2:0]));  // open: en
  Multiplexer #(.select(3), .width(32)) multiplexer_8 (
    .in0(register_3_q), .in1(register_7_q), .in2(register_11_q), .in3(register_15_q), .in4(register_19_q),
    .in5(register_23_q), .in6(register_27_q), .in7(register_31_q), .out(multiplexer_8_out), .sel(A2[2:0]));  // open: en
  Multiplexer #(.select(3), .width(32)) multiplexer_9 (
    .in0(register_4_q), .in1(register_8_q), .in2(register_12_q), .in3(register_16_q), .in4(register_20_q),
    .in5(register_24_q), .in6(register_28_q), .in7(register_32_q), .out(multiplexer_9_out), .sel(A2[2:0]));  // open: en
  Multiplexer #(.select(2), .width(32)) multiplexer_10 (
    .in0(multiplexer_2_out), .in1(multiplexer_3_out), .in2(multiplexer_4_out), .in3(multiplexer_5_out),
    .out(RD1), .sel(A1[4:3]));  // open: en
  Multiplexer #(.select(2), .width(32)) multiplexer_11 (
    .in0(multiplexer_6_out), .in1(multiplexer_7_out), .in2(multiplexer_8_out), .in3(multiplexer_9_out),
    .out(RD2), .sel(A2[4:3]));  // open: en
  // Probe on nothing
endmodule

// alu
module ALU (
  input  [31:0] a1,
  input  [31:0] a2,
  input  [1:0] aluop,
  output zero,
  output [31:0] aluout,
  output sign,
  output unsign
);

  wire [31:0] adder_1_out, and_1_out, or_1_out, subtractor_1_out;

  Adder #(.width(32)) adder_1 (.a(a1), .b(a2), .out(adder_1_out));  // open: cin, cout
  Subtractor #(.width(32)) subtractor_1 (.a(a1), .b(a2), .out(subtractor_1_out));  // open: bin, bout
  assign or_1_out = a1 | a2;  // OR_Gate or_1, 32 bits wide
  assign and_1_out = a1 & a2;  // AND_Gate and_1, 32 bits wide
  Comparator #(.width(32)) comparator_1 (.a(a1), .b(a2), .eq(zero));  // open: gt, lt
  Multiplexer #(.select(2), .width(32)) multiplexer_1 (
    .in0(and_1_out), .in1(adder_1_out), .in2(subtractor_1_out), .in3(or_1_out), .out(aluout), .sel(aluop));  // open: en
endmodule

module EXT (
  input  [15:0] A,
  input  [1:0] Extop,
  output [31:0] B
);

  wire [31:0] bit_extender_1_out, bit_extender_2_out;

  assign bit_extender_1_out = {{16{1'b0}}, A};  // Bit_Extender bit_extender_1
  assign bit_extender_2_out = {{16{A[15]}}, A};  // Bit_Extender bit_extender_2
  Multiplexer #(.select(2), .width(32)) multiplexer_1 (
    .in0(bit_extender_1_out), .in1(bit_extender_2_out), .in2({A, {16{1'b0}}}), .out(B), .sel(Extop));  // open: in3, en
endmodule

module NPC (
  input  [1:0] npcop,
  input  [31:0] pc4,
  input  [31:0] extout,
  input  [31:0] rd1,
  input  [31:0] instr,
  output [31:0] npc
);

  wire [31:0] adder_1_out, shifter_1_out, subtractor_1_out;

  Shifter #(.width(32)) shifter_1 (.in(extout), .\dist (5'b00010), .out(shifter_1_out));
  Subtractor #(.width(32)) subtractor_1 (.a(pc4), .b(32'h4), .out(subtractor_1_out));  // open: bin, bout
  Adder #(.width(32)) adder_1 (.a(pc4), .b(shifter_1_out), .out(adder_1_out));  // open: cin, cout
  Multiplexer #(.select(2), .width(32)) multiplexer_1 (
    .in0(adder_1_out), .in1({subtractor_1_out[31:28], instr[25:0], 2'b00}), .in2(rd1), .out(npc), .sel(npcop));  // open: in3, en
endmodule

module SHIFT (
  input  [1:0] shiftop,
  input  [4:0] shamt,
  input  [31:0] data,
  output [31:0] shiftdata
);

  wire [31:0] shifter_1_out, shifter_2_out, shifter_3_out;

  Shifter #(.width(32)) shifter_1 (.in(data), .\dist (shamt), .out(shifter_1_out));
  Shifter #(.width(32), .shift("lr")) shifter_2 (.in(data), .\dist (shamt), .out(shifter_2_out));
  Shifter #(.width(32), .shift("ar")) shifter_3 (.in(data), .\dist (shamt), .out(shifter_3_out));
  Multiplexer #(.select(2), .width(32)) multiplexer_1 (
    .in0(shifter_1_out), .in1(shifter_2_out), .in2(shifter_3_out), .out(shiftdata), .sel(shiftop));  // open: in3, en
endmodule

// control
module ctrl (
  input  [5:0] op,
  input  [5:0] funct,
  output [1:0] regdst,
  output regwrite,
  output alusrc,
  output [1:0] aluop,
  output memwrite,
  output [1:0] extop,
  output [1:0] npcop,
  output isbeq,
  output isbgtz,
  output isbgez,
  output isbltz,
  output isblez,
  output branch,
  output [2:0] memtoreg,
  output [1:0] dmdatactrl,
  output [1:0] sftop,
  output [1:0] dmoutctrl
);

  wire addi, addu, j, jal, jarl, jr, lbu, lhu, lui, lw, not_1_out, not_2_out, not_3_out, not_4_out,
       not_5_out, not_6_out, not_7_out, not_8_out, not_9_out, not_10_out, not_11_out, not_12_out, or_5_out,
       or_6_out, or_7_out, or_8_out, or_9_out, or_10_out, or_11_out, ori, sb, sh, sll, slt, special, sra,
       srl, subu, sw;

  not not_1 (not_1_out, op[4]);
  not not_2 (not_2_out, op[5]);
  not not_3 (not_3_out, op[3]);
  not not_4 (not_4_out, op[2]);
  not not_5 (not_5_out, op[1]);
  buf or_1 (dmdatactrl[1], sb);  // OR_Gate
  buf or_2 (dmdatactrl[0], sh);  // OR_Gate
  buf or_3 (dmoutctrl[1], lbu);  // OR_Gate
  buf or_4 (dmoutctrl[0], lhu);  // OR_Gate
  not not_6 (not_6_out, op[0]);
  and bgez (isbgez, not_2_out, not_1_out, not_3_out, not_4_out, not_5_out, op[0]);
  and bgtz (isbgtz, not_2_out, not_1_out, not_3_out, op[2], op[1], op[0]);
  and bltz (isbltz, not_2_out, not_1_out, not_3_out, not_4_out, not_5_out, op[0]);
  and blez (isblez, not_2_out, not_1_out, not_3_out, op[2], op[1], not_6_out);
  and u_special (special, not_2_out, not_1_out, not_3_out, not_4_out, not_5_out, not_6_out);
  and u_ori (ori, not_2_out, not_1_out, op[3], op[2], not_5_out, op[0]);
  and u_lw (lw, op[5], not_1_out, not_3_out, not_4_out, op[1], op[0]);
  and u_sw (sw, op[5], not_1_out, op[3], not_4_out, op[1], op[0]);
  and u_lui (lui, not_2_out, not_1_out, op[3], op[2], op[1], op[0]);
  and beq (isbeq, not_2_out, not_1_out, not_3_out, op[2], not_5_out, not_6_out);
  and u_j (j, not_2_out, not_1_out, not_3_out, not_4_out, op[1], not_6_out);
  and u_jal (jal, not_2_out, not_1_out, not_3_out, not_4_out, op[1], op[0]);
  and u_lhu (lhu, op[5], not_1_out, not_3_out, op[2], not_5_out, op[0]);
  and u_lbu (lbu, op[5], not_1_out, not_3_out, op[2], not_5_out, not_6_out);
  and u_sb (sb, op[5], not_1_out, op[3], not_4_out, not_5_out, not_6_out);
  and u_sh (sh, op[5], not_1_out, op[3], not_4_out, not_5_out, op[0]);
  and u_addi (addi, not_2_out, not_1_out, op[3], not_4_out, not_5_out, not_6_out);
  and u_addu (addu, funct[5], not_8_out, not_9_out, not_10_out, not_11_out, funct[0], special);
  and u_subu (subu, funct[5], not_8_out, not_9_out, not_10_out, funct[1], funct[0], special);
  and u_jr (jr, not_7_out, not_8_out, funct[3], not_10_out, not_11_out, not_12_out, special);
  and u_sll (sll, not_7_out, not_8_out, not_9_out, not_10_out, not_11_out, not_12_out, special);
  and u_srl (srl, not_7_out, not_8_out, not_9_out, not_10_out, funct[1], not_12_out, special);
  and u_sra (sra, not_7_out, not_8_out, not_9_out, not_10_out, funct[1], funct[0], special);
  and u_jarl (jarl, not_7_out, not_8_out, funct[3], not_10_out, not_11_out, funct[0], special);
  and u_slt (slt, funct[5], not_8_out, funct[3], not_10_out, funct[1], not_12_out, special);
  or or_5 (or_5_out, lhu, lbu, sb, sh);
  or or_6 (or_6_out, jarl, sll, srl, sra, lhu, lbu, or_7_out);
  or or_7 (or_7_out, addi, slt);
  or or_8 (or_8_out, lhu, lbu, sb, sh);
  or or_9 (or_9_out, isbgez, isbgtz, isbltz, isbeq, isblez);
  not not_7 (not_7_out, funct[5]);
  or or_10 (or_10_out, lhu, lbu, sb, sh);
  or or_11 (or_11_out, isbgez, isbgtz, isbltz, isblez, isbeq);
  not not_8 (not_8_out, funct[4]);
  buf or_12 (regdst[1], jal);  // OR_Gate
  or or_13 (regdst[0], ori, lw, lui, lhu, lbu, addi);
  or or_14 (regwrite, addu, subu, ori, lw, lui, jal, or_6_out);
  or or_15 (alusrc, ori, lw, sw, addi, or_5_out);
  or or_16 (aluop[1], subu, ori);
  buf or_17 (sftop[1], sra);  // OR_Gate
  buf or_18 (sftop[0], srl);  // OR_Gate
  not not_9 (not_9_out, funct[3]);
  or or_19 (aluop[0], addu, ori, lw, sw, addi, or_8_out);
  or or_20 (memwrite, sw, sb, sh);
  buf or_21 (extop[1], lui);  // OR_Gate
  or or_22 (extop[0], lw, sw, addi, or_9_out, or_10_out);
  or or_23 (npcop[1], jr, jarl);
  or or_24 (npcop[0], j, jal);
  or or_25 (branch, or_11_out, j, jal, jr, jarl);
  or or_26 (memtoreg[2], sll, srl, sra, slt);
  or or_27 (memtoreg[1], lui, jarl, jal);
  or or_28 (memtoreg[0], slt, lw, lhu, jal, lbu, jarl);
  not not_10 (not_10_out, funct[2]);
  not not_11 (not_11_out, funct[1]);
  not not_12 (not_12_out, funct[0]);
  // Probe on nothing

  // Other names for the same wires on the sheet: beq = isbeq; bgez = isbgez; bgtz = isbgtz; blez = isblez;
  //   bltz = isbltz
endmodule

module \byte  (
  input  [1:0] addr,
  input  [31:0] dmout,
  input  [31:0] data,
  output [31:0] byteout,
  output [31:0] fordmdata
);

  wire decoder_1_out0, decoder_1_out1, decoder_1_out2, decoder_1_out3;
  wire [7:0] multiplexer_1_out;

  Multiplexer #(.select(2), .width(8)) multiplexer_1 (
    .in0(dmout[7:0]), .in1(dmout[15:8]), .in2(dmout[23:16]), .in3(dmout[31:24]), .out(multiplexer_1_out),
    .sel(addr));  // open: en
  Decoder #(.select(2)) decoder_1 (
    .out0(decoder_1_out0), .out1(decoder_1_out1), .out2(decoder_1_out2), .out3(decoder_1_out3), .sel(addr));  // open: en
  assign byteout = {{24{1'b0}}, multiplexer_1_out};  // Bit_Extender bit_extender_1
  Multiplexer #(.width(8)) multiplexer_2 (
    .in0(dmout[7:0]), .in1(data[7:0]), .out(fordmdata[7:0]), .sel(decoder_1_out0));  // open: en
  Multiplexer #(.width(8)) multiplexer_3 (
    .in0(dmout[15:8]), .in1(data[7:0]), .out(fordmdata[15:8]), .sel(decoder_1_out1));  // open: en
  Multiplexer #(.width(8)) multiplexer_4 (
    .in0(dmout[23:16]), .in1(data[7:0]), .out(fordmdata[23:16]), .sel(decoder_1_out2));  // open: en
  Multiplexer #(.width(8)) multiplexer_5 (
    .in0(dmout[31:24]), .in1(data[7:0]), .out(fordmdata[31:24]), .sel(decoder_1_out3));  // open: en
endmodule

// half
module halfword (
  input  [1:0] addr,
  input  [31:0] dmout,
  input  [31:0] data,
  output [31:0] halfword,
  output [31:0] fordmdata
);

  wire not_1_out;
  wire [15:0] multiplexer_3_out;

  Multiplexer #(.width(16)) multiplexer_1 (
    .in0(dmout[15:0]), .in1(data[15:0]), .out(fordmdata[15:0]), .sel(not_1_out));  // open: en
  not not_1 (not_1_out, addr[1]);
  Multiplexer #(.width(16)) multiplexer_2 (
    .in0(dmout[31:16]), .in1(data[15:0]), .out(fordmdata[31:16]), .sel(addr[1]));  // open: en
  Multiplexer #(.width(16)) multiplexer_3 (
    .in0(dmout[15:0]), .in1(dmout[31:16]), .out(multiplexer_3_out), .sel(addr[1]));  // open: en
  assign halfword = {{16{1'b0}}, multiplexer_3_out};  // Bit_Extender bit_extender_1
endmodule

// cmp
module CMP (
  input  [31:0] A,
  input  [31:0] B,
  output BGTZ,
  output BGEZ,
  output BLEZ,
  output BLTZ
);

  wire comparator_1_eq;

  Comparator #(.width(32)) comparator_1 (.a(A), .b(B), .gt(BGTZ), .eq(comparator_1_eq), .lt(BLTZ));
  or or_1 (BGEZ, BGTZ, comparator_1_eq);
  or or_2 (BLEZ, comparator_1_eq, BLTZ);
endmodule

// branchlogic
module BRANCHLOGIC (
  input  isbgtz,
  input  isblez,
  input  isbgez,
  input  isbgtz_2,
  input  isbeq,
  input  bltz,
  input  blez,
  input  bgez,
  input  bgtz,
  input  zero,
  input  branch,
  output out_12
);

  wire and_1_out, and_2_out, and_3_out, and_4_out, and_5_out, and_6_out, not_1_out, or_2_out;

  or or_1 (out_12, and_1_out, and_2_out, and_3_out, and_4_out, and_5_out, and_6_out);
  and and_1 (and_1_out, branch, not_1_out);
  and and_2 (and_2_out, branch, isbgtz, bltz);
  and and_3 (and_3_out, branch, isblez, blez);
  and and_4 (and_4_out, branch, isbgez, bgez);
  and and_5 (and_5_out, branch, isbgtz_2, bgtz);
  and and_6 (and_6_out, branch, isbeq, zero);
  not not_1 (not_1_out, or_2_out);
  or or_2 (or_2_out, isbgtz, isblez, isbgez, isbgtz_2, isbeq);

  // Other names for the same wires on the sheet: ISBGTZ_t = isbgtz_2; ISBLTZ = isbgtz
endmodule
